# Fritzing sketch Tuan 3 bai 4 (saved by Fritzing 0.9.5d)
breadboards: 1

parts:
  R1 = Resistor [tolerance=±5% resistance=220 package=THT]
  LED1 = LED - 5mm [color="Red (633nm)" package="5 mm [THT]"]
  U1 = ESP32-38PinWide [part_number=ESP32-38PinWide]

nets:
  N1: R1.Pin_1, U1.GPIO22
  N2: LED1.cathode, U1.GND

custom parts:
  ESP32-38PinWide: Generic 38-Pin ESP32 with wide format (only access to one side of pins on a breadboard) based on Stephen Lilley's HiLetgo ESP-WROOM-32 ESP32 ESP-32S Development Board.
